# Fritzing sketch HumanHand2 (saved by Fritzing 0.9.3b)
breadboards: 4

parts:
  Composant1 = SparkFun ESP8266 Thing
  SparkFun_74HC4051_8-Channel_Mux_Breakout1 = SparkFun-74HC4051-8-Channel-Mux-Breakout [part_number=BOB-13906]
  R1 = Basic Flex Resistor
  R2 = Basic Flex Resistor
  R3 = Basic Flex Resistor
  R4 = Basic Flex Resistor
  R5 = Basic Flex Resistor
  R6 = Resistor [tolerance=±5% resistance=47k package="0402 [SMD]"]
  R8 = Resistor [tolerance=±5% resistance=47k package="0402 [SMD]"]
  R9 = Resistor [tolerance=±5% resistance=47k package="0402 [SMD]"]
  R10 = Resistor [tolerance=±5% resistance=47k package="0402 [SMD]"]
  R11 = Resistor [tolerance=±5% resistance=47k package="0402 [SMD]"]
  Composant2 = SparkFun ESP8266 Thing  # not connected
  J2 = Basic Servo
  J3 = Basic Servo
  J4 = Basic Servo
  J6 = Basic Servo  # not connected
  J5 = Basic Servo
  GY2 = MPU-6050 Board GY-521 [form="♀ (female)" package=THT]
  GY3 = MPU-6050 Board GY-521 [form="♀ (female)" package=THT]

nets:
  GND: Composant1.GND, SparkFun_74HC4051_8-Channel_Mux_Breakout1.GND, R6.Pin_0, R8.Pin_0, R9.Pin_0, R10.Pin_0, R11.Pin_0, GY2.pin2, GY3.pin2
  N1: Composant1.VCC, SparkFun_74HC4051_8-Channel_Mux_Breakout1.!E!, R1.Pin_2, R2.Pin_2, R3.Pin_2, R4.Pin_2, R5.Pin_2, GY2.pin1, GY3.pin1, GY3.pin7
  N2: Composant1.GPIO2, GY2.pin4, GY3.pin4
  N3: Composant1.GPIO14, GY2.pin3, GY3.pin3
  VIN: Composant1.VIN, SparkFun_74HC4051_8-Channel_Mux_Breakout1.VCC
  N4: Composant1.GPIO5, SparkFun_74HC4051_8-Channel_Mux_Breakout1.S0
  N5: Composant1.GPIO0, SparkFun_74HC4051_8-Channel_Mux_Breakout1.S1
  N6: Composant1.GPIO4, SparkFun_74HC4051_8-Channel_Mux_Breakout1.S2
  N7: Composant1.ADC, SparkFun_74HC4051_8-Channel_Mux_Breakout1.Z
  N8: SparkFun_74HC4051_8-Channel_Mux_Breakout1.Y4, R1.pin_1, R6.Pin_1
  N9: SparkFun_74HC4051_8-Channel_Mux_Breakout1.Y3, R2.pin_1, R11.Pin_1
  N10: SparkFun_74HC4051_8-Channel_Mux_Breakout1.Y2, R5.pin_1, R10.Pin_1
  N11: SparkFun_74HC4051_8-Channel_Mux_Breakout1.Y1, R4.pin_1, R9.Pin_1
  N12: SparkFun_74HC4051_8-Channel_Mux_Breakout1.Y0, R3.pin_1, R8.Pin_1
  GND_2: J2.gnd, J3.gnd, J4.gnd, J5.gnd
  VCC: J2.vcc, J3.vcc, J4.vcc, J5.vcc

notes:
  Les branchements des flex-sensors ne vont pas changer
  - alimentation vcc et gnd peuvent changer (sur la main humaine et cobot)
  - alimentation des servos également (dépends du voltage des servo)
  en attente de la partie alimentation (avec relais).
  Main Humaine
  est présent 5 flex sensors (1par doigt) : plus le flex-sensor est courbé ,moins le voltage est important
  2 MPU6050 (pousse & dessus du poignet)
  récupération des valeurs analogiques de chaque flex sur multiplexeur
  traitement
  communication TCP/IP à l'autre ESP
  Cobot
  On peut mettre 2 capteurs sur le bus i2c.
  Pour cela, il suffit d’agir sur la broche AD0 :
  si AD0=0 (ou laissé en l’air) : l’adresse du capteur en hexadécimal est 0x68,
  si AD0=1, l’adresse du capteur en hexadécimal est 0x69

custom parts:
  MPU-6050 Board GY-521: Acelerometro y Giroscopio MPU-6050 Board GY-521
